# Fritzing sketch aw_101_alarm (saved by Fritzing 0.6.3b)
breadboards: 1

parts:
  Arduino_Ethernet_Shield1 = Arduino Ethernet Shield
  R1 = Rotary Potentiometer (Small) [maximum_resistance=100kΩ]
  S1 = Toggle Switch [package=THT]
  R2 = Resistor [tolerance=±5% resistance=220 package=THT]

nets:
  N1: Arduino_Ethernet_Shield1.D2, S1.COM
  N2: Arduino_Ethernet_Shield1.+5V, R1.leg2, R2.Pin_0
  N3: Arduino_Ethernet_Shield1.GND, R1.leg1, S1.L1
  N4: Arduino_Ethernet_Shield1.A0, R1.wiper
  N5: S1.L2, R2.Pin_1
